// Logisim project first.circ as structural Verilog: 1 circuit, main circuit main
module main (
  input  A,
  input  B,
  input  VEM,
  input  in_4,
  input  in_5,
  input  in_6,
  input  in_7,
  input  in_8,
  input  in_9,
  input  in_10,
  output out_11,
  output out_12,
  output out_13,
  output out_14
);

  wire and_1_out, and_2_out, and_3_out, and_4_out, and_5_out, and_6_out, clock_1_out, or_2_out, xor_1_out;

  and and_1 (and_1_out, A, B);
  and and_2 (and_2_out, B, VEM);
  and and_3 (and_3_out, A, VEM);
  xor xor_1 (xor_1_out, A, B);
  Clock clock_1 (.out(clock_1_out));
  xor xor_2 (out_12, xor_1_out, VEM);
  or or_1 (out_11, and_1_out, and_2_out, and_3_out);
  Shift_Register shift_register_1 (
    .shift(in_5), .in(in_6), .clk(clock_1_out), .out(out_13), .load(in_4), .clr(in_7), .d0(in_4), .d1(in_4),
    .d2(in_4), .d3(in_4), .d4(in_4), .d5(in_4), .d6(in_4), .d7(in_4));  // open: q0, q1, q2, q3, q4, q5, q6, q7
  and and_4 (and_4_out, ~in_8, in_10);  // AND_Gate
  and and_5 (and_5_out, in_8, in_9);
  and and_6 (and_6_out, ~in_9, in_10);  // AND_Gate
  or or_2 (or_2_out, and_4_out, and_5_out);
  or or_3 (out_14, or_2_out, and_6_out);
endmodule
