// Logisim project atividade-circuitos-logicos.circ as structural Verilog: 1 circuit, main circuit main
module main (
  input  A,
  input  A_2,
  input  B,
  input  C,
  input  B_2,
  input  A_3,
  input  B_3,
  input  C_2,
  input  A_4,
  input  B_4,
  input  C_3,
  input  D,
  input  A_5,
  input  B_5,
  input  C_4,
  input  D_2,
  input  A_6,
  input  B_6,
  input  C_5,
  input  D_3,
  input  A_7,
  input  B_7,
  input  C_6,
  input  D_4,
  output out_25,
  output out_26,
  output out_27,
  output out_28,
  output out_29,
  output out_30
);

  wire and_1_out, and_2_out, and_3_out, and_4_out, and_5_out, and_6_out, and_7_out, and_9_out, and_10_out,
       and_11_out, not_1_out, not_2_out, not_3_out, not_4_out, not_5_out, not_7_out, not_8_out, not_9_out,
       not_10_out, or_1_out, or_2_out, or_4_out, or_6_out, or_7_out, or_8_out;

  not not_1 (not_1_out, A);
  not not_2 (not_2_out, C_2);
  not not_3 (not_3_out, A_3);
  not not_4 (not_4_out, D_3);
  not not_5 (not_5_out, C_6);
  or or_1 (or_1_out, not_1_out, B_2);
  // Probe on or_1_out
  and and_1 (and_1_out, A_3, C_2);
  and and_2 (and_2_out, B_3, not_2_out);
  and and_3 (and_3_out, not_3_out, B_3, C_2);
  and and_4 (and_4_out, A_6, B_6);
  and and_5 (and_5_out, C_5, not_4_out);
  and and_6 (and_6_out, A_7, B_7, not_5_out);
  or or_2 (or_2_out, A_7, B_7, C_6);
  and and_7 (and_7_out, or_2_out, D_4);
  or or_3 (out_26, and_1_out, and_2_out, and_3_out);
  or or_4 (or_4_out, and_4_out, and_5_out);
  not not_6 (out_28, or_4_out);
  or or_5 (out_30, and_6_out, and_7_out);
  not not_7 (not_7_out, B);
  or or_6 (or_6_out, A_2, B);
  or or_7 (or_7_out, not_7_out, C);
  not not_8 (not_8_out, B_5);
  not not_9 (not_9_out, C_4);
  and and_8 (out_25, or_6_out, or_7_out);
  and and_9 (and_9_out, C_3, D);
  and and_10 (and_10_out, A_5, not_8_out, not_9_out);
  and and_11 (and_11_out, A_5, B_5, D_2);
  not not_10 (not_10_out, D_2);
  or or_8 (or_8_out, B_4, and_9_out);
  or or_9 (out_29, and_10_out, and_11_out, not_10_out);
  and and_12 (out_27, or_8_out, A_4);

  // Notes on the sheet:
  //   a) F = ~A + B
  //   e) F = ~(AB + C~D)
  //   b) F = AC + B~C + ~ABC
  //   g) F = AB~C + (A+B+C)D
  //   c) F = (A+ B)(~B + C)
  //   d) F = A(B + CD)
  //   f) F =A~B~C + ABD + ~D
  //   Integrantes
  //   Alexandre Silva RA:624071
  //   Gabriela Stela Ramos RA:628751
  //   Hugo Hakamada Miyahara RA:626082
endmodule
